# Fritzing sketch Diagrama Robot (saved by Fritzing 0.9.2b)
breadboards: 1

parts:
  U1 = ESP8266 WiFi Module [part_number=ESP8266]
  Parte2 = Arduino Uno (Rev3) - ICSP
  S1 = H-Bridge with L298N
  S2 = H-Bridge with L298N
  M1 = DC Motor
  M2 = DC Motor
  M4 = DC Motor
  M5 = DC Motor
  U2 = LIPO-2000mAh [package=lipo-2000]

nets:
  VCC: U1.VCC, U1.RST, U1.CH_PD, U1.TXD, Parte2.3V3
  N1: U1.GPIO_0, U1.GPIO_2, Parte2.D4, Parte2.D5_PWM
  GND: U1.GND, Parte2.GND, S1.GND, S2.GND, U2.-
  N2: Parte2.D8, S1.IN2
  N3: Parte2.D9_PWM, S1.IN1
  N4: Parte2.D10_PWM/SS, S2.IN4
  N5: Parte2.D11_PWM/MOSI, S2.IN3
  N6: Parte2.D12/MISO, S2.IN2
  N7: Parte2.D13/SCK, S2.IN1
  N8: Parte2.D6_PWM, S1.IN4
  N9: Parte2.D7, S1.IN3
  12V: Parte2.VIN, S1.12V, S2.12V, U2.+
  N10: S1.OUT3-Motor2, M1.pin_2
  N11: S1.OUT4-Motor2, M1.pin_1
  N12: S1.OUT1-Motor1, M2.pin_2
  N13: S1.OUT2-Motor1, M2.pin_1
  N14: S2.OUT3-Motor2, M5.pin_2
  N15: S2.OUT4-Motor2, M5.pin_1
  N16: S2.OUT1-Motor1, M4.pin_1
  N17: S2.OUT2-Motor1, M4.pin_2

custom parts:
  ESP8266 WiFi Module: Generic WiFi Module based on the ESP8266 with onboard PCB antenna and UART communications
  H-Bridge with L298N: h-bridge
